// Digital circuit 8bitsCPU.dig as structural Verilog
module _8bitsCPU (
  input  clk,
  input  clk_2,
  input  clk_3,
  input  clk_4,
  input  clk_5,
  input  clk_6,
  input  clk_7,
  input  clk_8,
  input  clk_9,
  input  in_10
);

  wire C_p, CE, comparator_1_eq, E_a, E_i, E_p, E_u, En_mq, L_a, L_b, L_i, L_m, L_mq, L_o;
  wire [0:0] dipswitch_1_out;
  wire [2:0] counter_1_out, S_u;
  wire [3:0] Data, MAR_q, Op, PC_out, W;
  wire [6:0] driver_3_out;
  wire [7:0] Acumulador_q, ALU_p4, ALU_p5, ramdualport_1_d, Reg_MQ_q, register_1_q, Registrador_B_q;

  Comparator #(.Bits(3)) comparator_1 (.a(counter_1_out), .b(3'b110), .eq(comparator_1_eq));  // open: gt, lt
  Counter #(.Bits(3)) counter_1 (.en(1'b1), .C(clk_9), .clr(comparator_1_eq), .out(counter_1_out));  // open: ovf
  Counter #(.Bits(4)) PC (.en(C_p), .C(clk_5), .clr(1'b0), .out(PC_out));  // open: ovf
  assign PC_out = E_p ? W : 4'bz;  // Driver driver_1
  Register #(.Bits(4)) MAR (.D(W), .C(clk_3), .en(~L_m), .Q(MAR_q));
  RAMDualPort #(.AddrBits(4), .Bits(8)) ramdualport_1 (
    .A(MAR_q), .Din({8{1'b0}}), .str(1'b0), .C(clk_6), .ld(CE), .D(ramdualport_1_d));
  Register #(.Bits(8)) IR (.D({4'b0000, W}), .C(clk_4), .en(~L_i), .Q({Op, Data}));
  assign ramdualport_1_d = E_a ? {4'b0000, W} : 8'bz;  // Driver driver_2
  DipSwitch dipswitch_1 (.out(dipswitch_1_out[0]));
  ROM #(.AddrBits(7), .Bits(16)) rom_1 (
    .A({Op, counter_1_out}), .sel(in_10),
    .D({L_mq, En_mq, C_p, E_p, L_m, CE, L_i, E_i, L_a, E_a, S_u, E_u, L_b, L_o}));
  assign {driver_3_out, dipswitch_1_out[0]} = E_i ? {4'b0000, W} : 8'bz;  // Driver driver_3
  Register #(.Bits(8)) Acumulador (.D({4'b0000, W}), .C(clk), .en(L_a), .Q(Acumulador_q));
  // ALU ALU: pin names not known; wires that end beside it: {4'b0000, W}, Acumulador_q, S_u, ALU_p4, ALU_p5
  Register #(.Bits(8)) Registrador_B (.D(ALU_p4), .C(clk_2), .en(L_b), .Q(Registrador_B_q));
  Register #(.Bits(8)) register_1 (.D({4'b0000, W}), .C(clk_7), .en(L_o), .Q(register_1_q));
  assign Acumulador_q = E_a ? {4'b0000, W} : 8'bz;  // Driver driver_4
  assign ALU_p5 = E_u ? {4'b0000, W} : 8'bz;  // Driver driver_5
  assign Registrador_B_q = L_b ? {4'b0000, W} : 8'bz;  // Driver driver_6
  Seven_Seg_Hex seven_seg_hex_1 (.d(register_1_q[7:4]), .dp(1'b0));
  Register #(.Bits(8)) Reg_MQ (.D(ALU_p4), .C(clk_8), .en(En_mq), .Q(Reg_MQ_q));
  Seven_Seg_Hex seven_seg_hex_2 (.d(register_1_q[3:0]), .dp(1'b0));
  assign Reg_MQ_q = L_mq ? {4'b0000, W} : 8'bz;  // Driver driver_7
  // also tied to GND on the sheet: {driver_3_out[0], driver_3_out[1], driver_3_out[2], driver_3_out[3], driver_3_out[4], driver_3_out[5], driver_3_out[6]}

  // Notes on the sheet:
  //   contents of rom_1 (hex, n*v repeats v):
  //   0,0,4
endmodule
