// Digital circuit CPU8bits.dig as structural Verilog
module CPU8bits (
  input  Clock
);

  wire Deq, Qe;
  wire [7:0] alu_1_p2, alu_1_p4, undriven;
  wire [10:0] register_1_q, rom_1_d;

  D_FF d_ff_1 (.D(Qe), .C(Clock), .Q(Deq), .nQ(Qe));
  ROM #(.AddrBits(8), .Bits(11)) rom_1 (.A(undriven), .sel(Qe), .D(rom_1_d));
  Register #(.Bits(11)) register_1 (.D(rom_1_d), .C(Clock), .en(Qe), .Q(register_1_q));
  // ALU alu_1: pin names not known; wires that end beside it: register_1_q[7:0], alu_1_p2, register_1_q[10:8], alu_1_p4
  Register #(.Bits(8)) register_2 (.D(alu_1_p4), .C(Clock), .en(Qe), .Q(alu_1_p2));
  Seven_Seg_Hex seven_seg_hex_1 (.d(alu_1_p2[3:0]), .dp(1'b0));
  Seven_Seg_Hex seven_seg_hex_2 (.d(alu_1_p2[7:4]), .dp(1'b0));

  // Notes on the sheet:
  //   contents of rom_1 (hex, n*v repeats v):
  //   2,302
endmodule
