// Digital circuit PC.dig as structural Verilog
module PC (
  input  CLK,
  input  E_p,
  output [7:0] Addr
);

  wire [7:0] Data;

  Register #(.Bits(8)) register_1 (.D(Data), .C(CLK), .en(E_p), .Q(Addr));
  // _8bitAdder _8bitadder_1: pin names not known; wires that end beside it: Addr, 8'h1, Data, 1'b0

  // Other names for the same wires on the sheet: Ad[7:0] = Addr
endmodule
